// Logisim project Practica4.circ as structural Verilog
module XOR (
  input  P,
  input  Q,
  output P_XOR_Q
);

  wire and_1_out, and_2_out, not_1_out, not_2_out;

  not not_1 (not_1_out, P);
  not not_2 (not_2_out, Q);
  and and_1 (and_1_out, not_1_out, Q);
  and and_2 (and_2_out, P, not_2_out);
  or or_1 (P_XOR_Q, and_1_out, and_2_out);

  // Notes on the sheet:
  //   Compuerta XOR
endmodule

// ALU
module ALU_1_bit_suma (
  input  Ci,
  input  [1:0] Op,
  input  A,
  input  B,
  output A_Op_B,
  output Ci_1
);

  wire and_1_out, and_2_out, and_3_out, or_1_out, xor_1_p_xor_q, xor_2_p_xor_q;

  and and_1 (and_1_out, B, A);
  and and_2 (and_2_out, A, B);
  or or_1 (or_1_out, A, B);
  XOR xor_1 (.P(A), .Q(B), .P_XOR_Q(xor_1_p_xor_q));
  and and_3 (and_3_out, Ci, xor_1_p_xor_q);
  or or_2 (Ci_1, and_1_out, and_3_out);
  XOR xor_2 (.P(Ci), .Q(xor_1_p_xor_q), .P_XOR_Q(xor_2_p_xor_q));
  Multiplexer #(.select(2)) multiplexer_1 (
    .in0(and_2_out), .in1(or_1_out), .in2(xor_2_p_xor_q), .out(A_Op_B), .sel(Op));  // open: in3, en

  // Notes on the sheet:
  //   ALU de 1 bit suma
  //   Operaciones
  //   00- AND
  //   01-OR
  //   10-SUMA
endmodule

module ALU_8_bits_suma (
  input  C0,
  input  [1:0] Op,
  input  [7:0] A,
  input  [7:0] B,
  output [7:0] A_op_B,
  output Acarramiento
);

  wire alu_1_bit_suma_1_ci_1, alu_1_bit_suma_2_ci_1, alu_1_bit_suma_3_ci_1, alu_1_bit_suma_4_ci_1,
       alu_1_bit_suma_5_ci_1, alu_1_bit_suma_6_ci_1, alu_1_bit_suma_7_ci_1;

  ALU_1_bit_suma alu_1_bit_suma_1 (
    .A(A[0]), .B(B[0]), .A_Op_B(A_op_B[0]), .Ci(C0), .Op(Op), .Ci_1(alu_1_bit_suma_1_ci_1));
  ALU_1_bit_suma alu_1_bit_suma_2 (
    .A(A[1]), .B(B[1]), .A_Op_B(A_op_B[1]), .Ci(alu_1_bit_suma_1_ci_1), .Op(Op), .Ci_1(alu_1_bit_suma_2_ci_1));
  ALU_1_bit_suma alu_1_bit_suma_3 (
    .A(A[2]), .B(B[2]), .A_Op_B(A_op_B[2]), .Ci(alu_1_bit_suma_2_ci_1), .Op(Op), .Ci_1(alu_1_bit_suma_3_ci_1));
  ALU_1_bit_suma alu_1_bit_suma_4 (
    .A(A[3]), .B(B[3]), .A_Op_B(A_op_B[3]), .Ci(alu_1_bit_suma_3_ci_1), .Op(Op), .Ci_1(alu_1_bit_suma_4_ci_1));
  ALU_1_bit_suma alu_1_bit_suma_5 (
    .A(A[4]), .B(B[4]), .A_Op_B(A_op_B[4]), .Ci(alu_1_bit_suma_4_ci_1), .Op(Op), .Ci_1(alu_1_bit_suma_5_ci_1));
  ALU_1_bit_suma alu_1_bit_suma_6 (
    .A(A[5]), .B(B[5]), .A_Op_B(A_op_B[5]), .Ci(alu_1_bit_suma_5_ci_1), .Op(Op), .Ci_1(alu_1_bit_suma_6_ci_1));
  ALU_1_bit_suma alu_1_bit_suma_7 (
    .A(A[6]), .B(B[6]), .A_Op_B(A_op_B[6]), .Ci(alu_1_bit_suma_6_ci_1), .Op(Op), .Ci_1(alu_1_bit_suma_7_ci_1));
  ALU_1_bit_suma alu_1_bit_suma_8 (
    .A(A[7]), .B(B[7]), .A_Op_B(A_op_B[7]), .Ci(alu_1_bit_suma_7_ci_1), .Op(Op), .Ci_1(Acarramiento));

  // Notes on the sheet:
  //   ALU de 8 bits suma
  //   Operaciones
  //   00- AND
  //   01-OR
  //   10-SUMA
endmodule

// RESTA
module ALU_1_bit_resta (
  input  Ci,
  input  [1:0] Op,
  input  A,
  input  B,
  output A_Op_B,
  output Ci_1,
  output Overflow
);

  wire and_1_out, and_2_out, and_3_out, and_4_out, and_5_out, not_1_out, not_2_out, not_3_out, or_1_out,
       xor_1_p_xor_q, xor_2_p_xor_q, xor_3_p_xor_q;

  not not_1 (not_1_out, A);
  and and_1 (and_1_out, B, A);
  XOR xor_1 (.P(1'b1), .Q(B), .P_XOR_Q(xor_1_p_xor_q));
  not not_2 (not_2_out, xor_1_p_xor_q);
  and and_2 (and_2_out, A, B);
  or or_1 (or_1_out, A, B);
  XOR xor_2 (.P(A), .Q(B), .P_XOR_Q(xor_2_p_xor_q));
  XOR xor_3 (.P(Ci), .Q(xor_2_p_xor_q), .P_XOR_Q(xor_3_p_xor_q));
  and and_3 (and_3_out, Ci, xor_2_p_xor_q);
  or or_2 (Ci_1, and_1_out, and_3_out);
  not not_3 (not_3_out, xor_3_p_xor_q);
  Multiplexer #(.select(2)) multiplexer_1 (
    .in0(and_2_out), .in1(or_1_out), .in2(xor_3_p_xor_q), .in3(xor_1_p_xor_q), .out(A_Op_B), .sel(Op));  // open: en
  and and_4 (and_4_out, not_2_out, not_1_out, xor_3_p_xor_q);
  and and_5 (and_5_out, not_3_out, xor_1_p_xor_q, A);
  or or_3 (Overflow, and_4_out, and_5_out);

  // Notes on the sheet:
  //   Operaciones
  //   00- AND
  //   01-OR
  //   10-SUMA
  //   11-RESTA
  //   ALU de 1 bit resta
endmodule

// ALU -
module ALU_8_bits_igualdad (
  input  [7:0] A,
  input  [7:0] B,
  output [7:0] A_op_B,
  output out_4,
  output out_5
);

  wire [7:0] alu_1_bit_resta_1_p1;

  // ALU_1_bit_resta alu_1_bit_resta_1: pin names not known; wires that end beside it: alu_1_bit_resta_1_p1[0], B[0], alu_1_bit_resta_1_p1[1], 1'b1, A_op_B[0], out_4, out_5, A_op_B[1], out_5
  // ALU_1_bit_resta alu_1_bit_resta_2: pin names not known; wires that end beside it: B[0], alu_1_bit_resta_1_p1[1], B[1], alu_1_bit_resta_1_p1[2], 1'b1, out_5, A_op_B[1], out_5, out_4, A_op_B[2]
  // ALU_1_bit_resta alu_1_bit_resta_3: pin names not known; wires that end beside it: alu_1_bit_resta_1_p1[2], B[2], alu_1_bit_resta_1_p1[3], 1'b1, A_op_B[2], out_5, out_4, A_op_B[3]
  // ALU_1_bit_resta alu_1_bit_resta_4: pin names not known; wires that end beside it: alu_1_bit_resta_1_p1[3], B[3], alu_1_bit_resta_1_p1[4], 1'b1, A_op_B[3], out_5, out_4, A_op_B[4]
  // ALU_1_bit_resta alu_1_bit_resta_5: pin names not known; wires that end beside it: alu_1_bit_resta_1_p1[4], B[4], alu_1_bit_resta_1_p1[5], 1'b1, A_op_B[4], out_5, out_4, A_op_B[5]
  // ALU_1_bit_resta alu_1_bit_resta_6: pin names not known; wires that end beside it: alu_1_bit_resta_1_p1[5], B[5], alu_1_bit_resta_1_p1[6], 1'b1, A_op_B[5], out_5, out_4, A_op_B[6]
  // ALU_1_bit_resta alu_1_bit_resta_7: pin names not known; wires that end beside it: alu_1_bit_resta_1_p1[6], B[6], alu_1_bit_resta_1_p1[7], 1'b1, A_op_B[6], out_5, out_4, A_op_B[7]
  // ALU_1_bit_resta alu_1_bit_resta_8: pin names not known; wires that end beside it: alu_1_bit_resta_1_p1[7], B[7], 1'b1, A_op_B[7], out_5, out_4

  // Notes on the sheet:
  //   ALU de 8 bits igualdad
  //   Significados
  //   00000000-Son iguales
  //   Cualquier otra cosa- Son diferentes
endmodule

module ALU_1_bit_NOR (
  input  Ci,
  input  [2:0] Op,
  input  A,
  input  B,
  output A_Op_B,
  output Ci_1,
  output Overflow
);

  wire and_1_out, and_2_out, and_3_out, and_4_out, and_5_out, not_1_out, not_2_out, not_3_out, not_4_out,
       or_1_out, xor_1_p_xor_q, xor_2_p_xor_q, xor_3_p_xor_q;

  not not_1 (not_1_out, A);
  and and_1 (and_1_out, B, A);
  XOR xor_1 (.P(1'b1), .Q(B), .P_XOR_Q(xor_1_p_xor_q));
  not not_2 (not_2_out, xor_1_p_xor_q);
  and and_2 (and_2_out, A, B);
  or or_1 (or_1_out, A, B);
  XOR xor_2 (.P(A), .Q(B), .P_XOR_Q(xor_2_p_xor_q));
  XOR xor_3 (.P(Ci), .Q(xor_2_p_xor_q), .P_XOR_Q(xor_3_p_xor_q));
  and and_3 (and_3_out, Ci, xor_2_p_xor_q);
  or or_2 (Ci_1, and_1_out, and_3_out);
  not not_3 (not_3_out, or_1_out);
  not not_4 (not_4_out, xor_3_p_xor_q);
  Multiplexer #(.select(3)) multiplexer_1 (
    .in0(and_2_out), .in1(or_1_out), .in2(xor_3_p_xor_q), .in3(xor_1_p_xor_q), .in4(not_3_out), .out(A_Op_B),
    .sel(Op));  // open: in5, in6, in7, en
  and and_4 (and_4_out, not_2_out, not_1_out, xor_3_p_xor_q);
  and and_5 (and_5_out, not_4_out, xor_1_p_xor_q, A);
  or or_3 (Overflow, and_4_out, and_5_out);

  // Notes on the sheet:
  //   Operaciones
  //   000- AND
  //   001-OR
  //   010-SUMA
  //   011-RESTA
  //   100-NOR
  //   ALU de 1 bit NOR
endmodule

module ALU_8_bits_NOR (
  input  [7:0] A,
  input  [7:0] B
);


  // Notes on the sheet:
  //   ALU de 8 bits NOR
endmodule
